# Fritzing sketch corrente (saved by Fritzing 0.9.2b)
breadboards: 1

parts:
  U1 = NodeMCU V3.0
  L1 = sct-013 [part_number=sct-013 package="4Ucon 08780 [THT]"]
  R1 = Resistor [tolerance=±5% resistance=330 package="0603 [SMD]"]
  R2 = Resistor [tolerance=±5% resistance=10k package="2010 [SMD]"]
  R3 = Resistor [tolerance=±5% resistance=10k package="2010 [SMD]"]
  C1 = Electrolytic Capacitor [capacitance=0.1mF package="0405 [SMD, electrolytic]"]
  KY-1 = Keyes Relay [package=THT]
  S1 = Round Pushbutton
  LED1 = LEDs [package=led10mm]

nets:
  N1: U1.D1, KY-1.power
  N2: U1.D2, S1.leg0
  N3: U1.GND#6, U1.GND#13, U1.GND#16, U1.GND#33, R2.Pin_0, C1.-, KY-1.ground, S1.leg1
  N4: U1.Vin, R3.Pin_1, KY-1.signal
  N5: U1.A0, L1.pin_0, R1.Pin_1
  N6: L1.pin_1, R1.Pin_0, R2.Pin_1, R3.Pin_0, C1.+
  N7: KY-1.NC, LED1.A

custom parts:
  NodeMCU V3.0: ESP8266 based NodeMCU
  sct-013: sct-013 Current transformer. The pcb footprint is from the 3.5mm stereo jack (as the sensor comes with a 3.5 mm stero plug).
  Keyes Relay: The Keyes 5V relay module is suitable for SCM development, home appliance control. It uses a 5V~12V TIL control signal which can control DC / AC signal.
  LEDs: LEDs Standard schematic elements and footprints for 5mm, 3mm, 1206, and 0603 sized LEDs. 5mm - Spark Fun Electronics SKU : COM-00529 (and others)
